// Logisim project Vechile_Parking_System.circ as structural Verilog: 1 circuit, main circuit main
module main (
  input  in_1,
  input  in_2,
  input  in_3,
  input  in_4,
  input  in_5,
  input  in_6,
  input  in_7,
  input  in_8,
  input  in_9,
  input  in_10,
  input  L_5_6f9a5918,
  input  in_12,
  input  in_13,
  input  L_2_9af3f3aa,
  input  in_15,
  input  in_16,
  input  in_17,
  input  in_18,
  input  in_19,
  input  in_20,
  input  in_21,
  input  in_22,
  input  in_23,
  input  in_24,
  input  in_25,
  input  L_6_8731f0b1,
  input  in_27,
  input  in_28,
  input  in_29,
  input  in_30,
  input  L_1_a634c1bf,
  input  in_32,
  input  L_7_e564d037,
  input  in_34,
  input  in_35,
  input  in_36,
  input  in_37,
  input  in_38,
  input  in_39,
  input  L_0_8bb39f3a,
  input  in_41,
  input  in_42,
  input  in_43,
  input  L_4_372cd2c5,
  input  L_3_c61f790f,
  input  in_46,
  input  in_47,
  input  in_48,
  output out_49,
  output out_50,
  output out_51,
  output out_52,
  output out_53,
  output out_54,
  output out_55,
  output out_56,
  output out_57,
  output out_58,
  output out_59,
  output out_60,
  output out_61,
  output out_62,
  output out_63,
  output out_64,
  output out_65,
  output out_66,
  output out_67,
  output out_68,
  output out_69,
  output out_70
);

  wire and_6_out, and_7_out, and_8_out, and_9_out, and_10_out, and_11_out, and_12_out, and_13_out,
       and_14_out, and_15_out, and_16_out, and_17_out, button_1_out, button_2_out, button_3_out,
       button_4_out, button_5_out, button_6_out, not_1_out, not_2_out, not_3_out, not_4_out, or_19_out,
       or_20_out, or_21_out, or_22_out, or_23_out, or_24_out, subtractor_2_bout, subtractor_3_bout,
       subtractor_4_bout, t_ff_3_q, t_ff_4_q, t_ff_7_q, t_ff_7_qn, t_ff_10_q, undriven, undriven_2,
       undriven_3, undriven_4, undriven_5, undriven_6, undriven_7, undriven_8, undriven_9, undriven_10;

  Button button_1 (.out(button_1_out));
  Button button_2 (.out(button_2_out));
  // AND_Gate and_1 is placed but not wired
  // AND_Gate and_2 is placed but not wired
  // AND_Gate and_3 is placed but not wired
  // AND_Gate and_4 is placed but not wired
  // AND_Gate and_5 is placed but not wired
  or or_1 (out_49, in_1, in_2, in_3, in_4);
  or or_2 (out_50, in_1, in_2, in_5, in_6);
  or or_3 (out_51, in_3, in_5);
  or or_4 (out_52, in_9, in_10, L_5_6f9a5918, in_12);
  or or_5 (out_53, in_9, in_10, in_13, L_2_9af3f3aa);
  or or_6 (out_54, in_9, L_5_6f9a5918, in_13, in_15);
  or or_7 (out_55, in_17, in_18, in_19, in_20);
  or or_8 (out_56, in_17, in_18, in_21, in_22);
  or or_9 (out_57, in_17, in_19, in_21, in_23);
  or or_10 (out_62, in_25, L_6_8731f0b1, in_27, in_28);
  or or_11 (out_63, in_25, L_6_8731f0b1, in_29, in_30);
  or or_12 (out_64, in_27, in_29);
  or or_13 (out_65, L_7_e564d037, in_34, in_35, in_36);
  or or_14 (out_66, L_7_e564d037, in_34, in_37, in_38);
  or or_15 (out_67, L_7_e564d037, in_35, in_37, in_39);
  or or_16 (out_68, in_41, in_42, in_43, L_4_372cd2c5);
  or or_17 (out_69, in_41, in_42, L_3_c61f790f, in_46);
  or or_18 (out_70, in_41, in_43, L_3_c61f790f, in_47);
  and and_6 (and_6_out, out_49, out_57);
  and and_7 (and_7_out, out_50, out_57);
  and and_8 (and_8_out, out_49, in_22);
  and and_9 (and_9_out, out_49, out_57);
  Button button_3 (.out(button_3_out));
  buf and_10 (and_10_out, out_49);  // AND_Gate
  Subtractor #(.width(1)) subtractor_1 (
    .a(undriven_2), .b(undriven), .out(out_58), .bin(subtractor_2_bout));  // open: bout
  T_Flip_Flop t_ff_1 (.clk(button_4_out), .reset(undriven_4), .preset(undriven_4));  // open: T, Q, Qn
  Button button_4 (.out(button_4_out));
  or or_19 (or_19_out, and_6_out, and_10_out);
  T_Flip_Flop t_ff_2 (.clk(button_3_out), .Qn(button_3_out), .preset(undriven_5));  // open: T, Q, reset
  and and_11 (and_11_out, out_62, out_70);
  and and_12 (and_12_out, out_63, out_70);
  and and_13 (and_13_out, out_62, in_46);
  and and_14 (and_14_out, out_62, out_70);
  buf and_15 (and_15_out, out_62);  // AND_Gate
  Button button_5 (.out(button_5_out));
  not not_1 (not_1_out, or_19_out);
  and and_16 (and_16_out, or_19_out, or_21_out);
  Subtractor #(.width(1)) subtractor_2 (
    .a(t_ff_7_q), .b(undriven_3), .out(out_59), .bin(subtractor_3_bout), .bout(subtractor_2_bout));
  Button button_6 (.out(button_6_out));
  or or_20 (or_20_out, and_11_out, and_15_out);
  or or_21 (or_21_out, undriven_4, undriven_6);
  LED led_1 (.in(not_3_out));
  or or_22 (or_22_out, not_1_out, not_3_out);
  LED led_2 (.in(or_22_out));
  LED led_3 (.in(and_16_out));
  T_Flip_Flop t_ff_3 (
    .clk(button_3_out), .Q(t_ff_3_q), .Qn(button_3_out), .reset(undriven_5), .preset(undriven_5));  // open: T
  Subtractor #(.width(1)) subtractor_3 (
    .a(undriven_9), .b(undriven_7), .out(out_60), .bin(subtractor_4_bout), .bout(subtractor_3_bout));
  T_Flip_Flop t_ff_4 (
    .clk(button_6_out), .Q(t_ff_4_q), .Qn(t_ff_4_q), .reset(undriven_8), .preset(undriven_8));  // open: T
  not not_2 (not_2_out, or_20_out);
  and and_17 (and_17_out, or_20_out, or_23_out);
  T_Flip_Flop t_ff_5 (.clk(button_5_out), .Qn(button_5_out), .preset(t_ff_4_q));  // open: T, Q, reset
  T_Flip_Flop t_ff_6 (.clk(button_4_out), .preset(undriven_6));  // open: T, Q, Qn, reset
  not not_3 (not_3_out, or_21_out);
  LED L_8_c4cdbe7c (.in(undriven_2));
  LED led_4 (.in(t_ff_7_q));
  T_Flip_Flop t_ff_7 (
    .clk(t_ff_3_q), .T(button_3_out), .Q(t_ff_7_q), .Qn(t_ff_7_qn), .reset(button_3_out));  // open: preset
  Subtractor #(.width(1)) subtractor_4 (
    .a(undriven_5), .b(t_ff_4_q), .out(out_61), .bout(subtractor_4_bout));  // open: bin
  or or_23 (or_23_out, undriven_8, undriven_10);
  or or_24 (or_24_out, not_2_out, not_4_out);
  T_Flip_Flop t_ff_8 (.clk(button_5_out), .Qn(button_5_out), .preset(undriven_7));  // open: T, Q, reset
  LED led_5 (.in(undriven_9));
  LED led_6 (.in(undriven_5));
  T_Flip_Flop t_ff_9 (.clk(button_6_out), .preset(undriven_10));  // open: T, Q, Qn, reset
  not not_4 (not_4_out, or_23_out);
  LED led_7 (.in(not_4_out));
  LED led_8 (.in(or_24_out));
  LED led_9 (.in(and_17_out));
  LED led_10 (.in(undriven));
  LED led_11 (.in(undriven_3));
  T_Flip_Flop t_ff_10 (.clk(button_5_out), .Q(t_ff_10_q), .Qn(button_5_out), .preset(undriven_3));  // open: T, reset
  T_Flip_Flop t_ff_11 (.clk(button_3_out), .reset(undriven_2), .preset(undriven_2));  // open: T, Q, Qn
  LED led_12 (.in(undriven_7));
  LED led_13 (.in(t_ff_4_q));
  T_Flip_Flop t_ff_12 (.clk(button_5_out), .reset(undriven), .preset(undriven));  // open: T, Q, Qn
  // also tied to VCC on the sheet: {button_5_out, button_3_out}

  // Notes on the sheet:
  //   ENTRY BUZZER
  //   1.722
  //   2.701
  //   3.217
  //   4.645
  //   5.420
  //   PASSWORDS
  //   EXIT BUZZER
  //   TOTAL NUMBER OF VEHICLES IN PARKING SLOT(binary form)
  //   LOGISIM FOR ENTRY AND EXIT OF TWO WHEELERS
  //   GATE IS CLOSED
  //   GATE IS OPENED :)
  //   ENTERED VEHICLE NUMBER(binary form)
  //   Your chance is over!!ACCESS DENIED
  //   GATE IS CLOSED
  //   GATE IS OPENED :)
  //   EXITTED VEHICLE NUMBER(Binary form)
  //   Your chance is over!!ACCESS DENIED
endmodule
